# Fritzing sketch schema-prototype (saved by Fritzing 0.9.3b)
breadboards: 1

parts:
  D1 = Rectifier Diode [part_number=1N4548 package="300 mil [THT]"]
  R1 = Resistor [tolerance=±5% resistance=10k package=THT]
  L1 = Inductor [inductance=10pH package="400 mil [THT]"]
  R2 = Resistor [tolerance=±5% resistance=3.3k package=THT]
  R3 = Resistor [tolerance=±5% resistance=1M package=THT]
  C2 = Ceramic Capacitor [capacitance=10nF package="100 mil [THT, multilayer]"]
  C1 = Ceramic Capacitor [capacitance=0.1nF package="100 mil [THT, multilayer]"]
  Composant1 = Arduino Uno (Rev3)
  LED1 = LED - 5mm [color="Red (633nm)" package="5 mm [THT]"]
  R4 = Resistor [tolerance=±5% resistance=220 package=THT]
  R5 = Resistor [tolerance=±5% resistance=220 package=THT]
  LED2 = LED - 5mm [color="Green (560nm)" package="5 mm [THT]"]
  LED3 = LED - 5mm [color="Yellow (585nm)" package="5 mm [THT]"]
  R6 = Resistor [tolerance=±5% resistance=220 package=THT]

nets:
  N1: D1.cathode, R3.Pin_1, C1.1, Composant1.A0
  N2: D1.anode, L1.pin_0, C2.0
  N3: R1.Pin_0, L1.pin_1, R2.Pin_1
  N4: R1.Pin_1, Composant1.D9_PWM
  GND: R2.Pin_0, Composant1.GND, LED1.cathode, LED2.cathode, LED3.cathode
  N5: R3.Pin_0, C1.0
  N6: Composant1.D3_PWM, R4.Pin_0
  N7: Composant1.D5_PWM, R6.Pin_0
  N8: Composant1.D7, R5.Pin_0
  N9: LED1.anode, R4.Pin_1
  N10: R5.Pin_1, LED2.anode
  N11: LED3.anode, R6.Pin_1
