# Fritzing sketch schèma 2 (saved by Fritzing 0.9.3b)
breadboards: 1

parts:
  D1 = Rectifier Diode [part_number=1N4548 package="300 mil [THT]"]
  R1 = Resistor [tolerance=±5% resistance=10k package=THT]
  L1 = Inductor [inductance=10pH package="400 mil [THT]"]
  R2 = Resistor [tolerance=±5% resistance=3.3k package=THT]
  R3 = Resistor [tolerance=±5% resistance=1M package=THT]
  C2 = Ceramic Capacitor [capacitance=10nF package="100 mil [THT, multilayer]"]
  C1 = Ceramic Capacitor [capacitance=0.1nF package="100 mil [THT, multilayer]"]
  Composant1 = Arduino Uno (Rev3)

nets:
  N1: D1.anode, L1.pin_0, C2.0
  N2: R1.Pin_0, L1.pin_1, R2.Pin_1
  N3: R1.Pin_1, Composant1.D9_PWM
  GND: R2.Pin_0, Composant1.GND
  N4: R3.Pin_0, C1.0
  N5: R3.Pin_1, C1.1, Composant1.A0
